// Logisim project Arquitetura Mips 32.circ as structural Verilog: 13 circuits, main circuit Completo
// PC
module main (
  input  Enable
);

  wire alu_1_zero, Clock_out, undriven, unidade_controle_1_alusrc, unidade_controle_1_atuapc,
       unidade_controle_1_branch, unidade_controle_1_jump, unidade_controle_1_memread,
       unidade_controle_1_memtoreg, unidade_controle_1_memwrite, unidade_controle_1_regdst,
       unidade_controle_1_regwrite;
  wire [1:0] unidade_controle_1_opalu;
  wire [2:0] alu_control_1_result;
  wire [4:0] decod_instru_1_rd, decod_instru_1_rs, decod_instru_1_rt, multiplexer_3_out;
  wire [5:0] decod_instru_1_funct, decod_instru_1_opcode;
  wire [15:0] decod_instru_1_immediate;
  wire [27:0] adder_1_out;
  wire [31:0] adder_2_out, alu_1_resultado, banco_registrador_1_dados_de_leitura_1,
       banco_registrador_1_dados_de_leitura_2, bit_extender_1_out, mem_dados_1_output, multiplexer_1_out,
       multiplexer_2_out, multiplexer_4_out, multiplexer_5_out, PC_q, shifter_1_out, undriven_2;
  wire [31:2] decod_instru_1_address;

  Clock Clock (.out(Clock_out));
  Multiplexer #(.width(32), .enable("false")) multiplexer_1 (
    .in0(adder_2_out), .in1(multiplexer_2_out), .out(multiplexer_1_out), .sel(unidade_controle_1_jump));
  Register #(.width(32)) PC (
    .D(multiplexer_1_out), .en(unidade_controle_1_atuapc), .Q(PC_q), .clk(Clock_out));  // open: clr
  Multiplexer #(.width(32), .enable("false")) multiplexer_2 (
    .in0({decod_instru_1_address, 2'b00}), .in1({decod_instru_1_address[31:28], adder_1_out}),
    .out(multiplexer_2_out), .sel(undriven));
  Adder #(.width(32)) adder_1 (
    .a(32'h4), .b(PC_q), .out({decod_instru_1_address[31:28], adder_1_out}));  // open: cin, cout
  \Memoria_Instrução  \memoria_instrução_1  (.PC(PC_q), .INSTRUCTION(undriven_2));  // open: AtuaPC
  Decod_instru decod_instru_1 (
    .Instruction(undriven_2), .OPCODE(decod_instru_1_opcode), .RS(decod_instru_1_rs), .RT(decod_instru_1_rt),
    .RD(decod_instru_1_rd), .FUNCT(decod_instru_1_funct), .IMMEDIATE(decod_instru_1_immediate),
    .ADDRESS(decod_instru_1_address[27:2]));
  Multiplexer #(.width(5), .enable("false")) multiplexer_3 (
    .in0(decod_instru_1_rt), .in1(decod_instru_1_rd), .out(multiplexer_3_out), .sel(unidade_controle_1_regdst));
  assign bit_extender_1_out = {{16{1'b0}}, decod_instru_1_immediate};  // Bit_Extender bit_extender_1
  unidade_controle unidade_controle_1 (
    .Enable(Enable), .RegDst(unidade_controle_1_regdst), .ALUSrc(unidade_controle_1_alusrc),
    .MemToReg(unidade_controle_1_memtoreg), .RegWrite(unidade_controle_1_regwrite),
    .MemRead(unidade_controle_1_memread), .MemWrite(unidade_controle_1_memwrite),
    .Branch(unidade_controle_1_branch), .OpALU(unidade_controle_1_opalu), .Jump(unidade_controle_1_jump),
    .Clock(Clock_out), .AtuaPC(unidade_controle_1_atuapc), .\Instrução (decod_instru_1_opcode));  // open: Branch_Not_Equal
  Banco_registrador banco_registrador_1 (
    .Read_Reg_1(decod_instru_1_rs), .Read_Reg_2(decod_instru_1_rt), .Enable(Enable),
    .Dados_de_Leitura_1(banco_registrador_1_dados_de_leitura_1),
    .Dados_de_Leitura_2(banco_registrador_1_dados_de_leitura_2), .Read_Write(multiplexer_3_out),
    .Escreve_Registrador(unidade_controle_1_regwrite), .CLK(Clock_out), .Dados_para_escrita(multiplexer_5_out));
  Shifter #(.width(32)) shifter_1 (.in(bit_extender_1_out), .\dist (5'b00010), .out(shifter_1_out));
  Multiplexer #(.width(32), .enable("false")) multiplexer_4 (
    .in0(banco_registrador_1_dados_de_leitura_2), .in1(bit_extender_1_out), .out(multiplexer_4_out),
    .sel(unidade_controle_1_alusrc));
  Adder #(.width(32)) adder_2 (
    .a({decod_instru_1_address[31:28], adder_1_out}), .b(shifter_1_out), .out(adder_2_out));  // open: cin, cout
  Multiplexer #(.width(32), .enable("false")) multiplexer_5 (
    .in0(alu_1_resultado), .in1(mem_dados_1_output), .out(multiplexer_5_out),
    .sel(unidade_controle_1_memtoreg));
  ALU_Control alu_control_1 (
    .FUNCAO(decod_instru_1_funct), .OPCode(unidade_controle_1_opalu), .Result(alu_control_1_result));
  ALU alu_1 (
    .A(banco_registrador_1_dados_de_leitura_1), .B(multiplexer_4_out), .RESULTADO(alu_1_resultado),
    .Zero(alu_1_zero), .Operacao(alu_control_1_result));
  Mem_Dados mem_dados_1 (
    .Resultado_da_ALU(alu_1_resultado), .Entrada_de_Dados(banco_registrador_1_dados_de_leitura_2),
    .Output(mem_dados_1_output), .Enable(Enable), .Le_Mem(unidade_controle_1_memread), .Clock(Clock_out),
    .Escreve_Mem(unidade_controle_1_memwrite));
endmodule

module \Memoria_Instrução  (
  input  [31:0] INSTRUCTION,
  input  [31:0] PC,
  input  AtuaPC
);

  wire [6:0] bitselector_1_out;

  BitSelector #(.width(30), .group(7)) bitselector_1 (.in(PC[31:2]), .out(bitselector_1_out), .sel(3'b000));
  RAM #(.addrWidth(7), .dataWidth(32)) ram_1 (
    .addr(bitselector_1_out), .data(INSTRUCTION), .sel(1'b1), .clk(AtuaPC), .ld(1'b1), .clr(1'b0));
endmodule

module Decod_instru (
  input  [31:0] Instruction,
  output [5:0] OPCODE,
  output [4:0] RS,
  output [4:0] RT,
  output [4:0] RD,
  output [5:0] FUNCT,
  output [15:0] IMMEDIATE,
  output [25:0] ADDRESS
);


  assign ADDRESS = Instruction[25:0];
  assign FUNCT = Instruction[5:0];
  assign IMMEDIATE = Instruction[15:0];
  assign OPCODE = Instruction[31:26];
  assign RD = Instruction[15:11];
  assign RS = Instruction[25:21];
  assign RT = Instruction[20:16];
endmodule

module ALU_Control (
  input  [5:0] FUNCAO,
  input  [1:0] OPCode,
  output [2:0] Result
);

  wire and_1_out;
  wire [2:0] bitselector_1_out, rom_1_data;

  ROM #(.addrWidth(6), .dataWidth(3)) rom_1 (.addr(FUNCAO), .data(rom_1_data));  // open: sel
  BitSelector #(.width(2), .group(3)) bitselector_1 (.in(OPCode), .out(bitselector_1_out), .sel(and_1_out));
  and and_1 (and_1_out, OPCode[0], OPCode[1]);
  Multiplexer #(.width(3), .enable("false")) multiplexer_1 (
    .in0(rom_1_data), .in1(bitselector_1_out), .out(Result), .sel(and_1_out));

  // Notes on the sheet:
  //   contents of rom_1 (hex, n*v repeats v):
  //   6 31*0 2 0 6 0 0 1 4*0 7
  //   add 100000
  //   sub 100010
  //   and 100100
  //   or 100101
  //   slt 101010
endmodule

module ALU (
  input  [2:0] Operacao,
  input  [31:0] A,
  input  [31:0] B,
  output [31:0] RESULTADO,
  output Zero
);

  wire [0:0] comparator_1_lt;
  wire [31:0] adder_1_out, and_1_out, multiplexer_1_out, multiplexer_2_out, not_1_out, not_2_out, or_1_out;

  assign not_1_out = ~A;  // NOT_Gate not_1, 32 bits wide
  assign not_2_out = ~B;  // NOT_Gate not_2, 32 bits wide
  Comparator #(.width(32)) comparator_1 (.a(A), .b(B), .lt(comparator_1_lt[0]));  // open: gt, eq
  Multiplexer #(.width(32), .enable("false")) multiplexer_1 (
    .in0(A), .in1(not_1_out), .out(multiplexer_1_out), .sel(Operacao[2]));
  Multiplexer #(.width(32), .enable("false")) multiplexer_2 (
    .in0(B), .in1(not_2_out), .out(multiplexer_2_out), .sel(Operacao[2]));
  assign and_1_out = multiplexer_1_out & multiplexer_2_out;  // AND_Gate and_1, 32 bits wide
  assign or_1_out = multiplexer_1_out | multiplexer_2_out;  // OR_Gate or_1, 32 bits wide
  Adder #(.width(32)) adder_1 (
    .a(multiplexer_1_out), .b(multiplexer_2_out), .out(adder_1_out), .cin(Operacao[2]));  // open: cout
  Multiplexer #(.select(2), .width(32), .enable("false")) multiplexer_3 (
    .in0(and_1_out), .in1(or_1_out), .in2(adder_1_out), .in3({{31{1'b0}}, comparator_1_lt[0]}),
    .out(RESULTADO), .sel(Operacao[1:0]));
  NotExactlyOne xnor_1 (
    .out(Zero), .in0(RESULTADO[0]), .in1(RESULTADO[1]), .in2(RESULTADO[2]), .in3(RESULTADO[3]),
    .in4(RESULTADO[4]), .in5(RESULTADO[5]), .in6(RESULTADO[6]), .in7(RESULTADO[7]), .in8(RESULTADO[8]),
    .in9(RESULTADO[9]), .in10(RESULTADO[10]), .in11(RESULTADO[11]), .in12(RESULTADO[12]),
    .in13(RESULTADO[13]), .in14(RESULTADO[14]), .in15(RESULTADO[15]), .in16(RESULTADO[16]),
    .in17(RESULTADO[17]), .in18(RESULTADO[18]), .in19(RESULTADO[19]), .in20(RESULTADO[20]),
    .in21(RESULTADO[21]), .in22(RESULTADO[22]), .in23(RESULTADO[23]), .in24(RESULTADO[24]),
    .in25(RESULTADO[25]), .in26(RESULTADO[26]), .in27(RESULTADO[27]), .in28(RESULTADO[28]),
    .in29(RESULTADO[29]), .in30(RESULTADO[30]), .in31(RESULTADO[31]));

  // Notes on the sheet:
  //   Operacao
  //   000
  //   001
  //   010
  //   110
  //   111
  //   Funçao
  //   and
  //   or
  //   soma
  //   sub
  //   set on less than
endmodule

module Banco_registrador (
  input  [4:0] Read_Reg_1,
  input  [4:0] Read_Reg_2,
  input  [31:0] Dados_para_escrita,
  input  CLK,
  input  Escreve_Registrador,
  input  Enable,
  input  [4:0] Read_Write,
  output [31:0] Dados_de_Leitura_1,
  output [31:0] Dados_de_Leitura_2
);

  wire _0_out, _1_out, _2_out, _3_out, _4_out, _5_out, _6_out, _7_out, _8_out, _9_out, _10_out, _11_out,
       _12_out, _13_out, _14_out, _15_out, _16_out, _17_out, _18_out, _19_out, _20_out, _21_out, _22_out,
       _23_out, _24_out, _25_out, _26_out, _27_out, _28_out, _29_out, _30_out, _31_out, decoder_1_out0,
       decoder_1_out1, decoder_1_out2, decoder_1_out3, decoder_1_out4, decoder_1_out5, decoder_1_out6,
       decoder_1_out7, decoder_1_out8, decoder_1_out9, decoder_1_out10, decoder_1_out11, decoder_1_out12,
       decoder_1_out13, decoder_1_out14, decoder_1_out15, decoder_1_out16, decoder_1_out17, decoder_1_out18,
       decoder_1_out19, decoder_1_out20, decoder_1_out21, decoder_1_out22, decoder_1_out23, decoder_1_out24,
       decoder_1_out25, decoder_1_out26, decoder_1_out27, decoder_1_out28, decoder_1_out29, decoder_1_out30,
       decoder_1_out31, decoder_2_out0, decoder_2_out1, not_1_out;
  wire [31:0] register_1_q, register_2_q, register_3_q, register_4_q, register_5_q, register_6_q,
       register_7_q, register_8_q, register_9_q, register_10_q, register_11_q, register_12_q, register_13_q,
       register_14_q, register_15_q, register_16_q, register_17_q, register_18_q, register_19_q,
       register_20_q, register_21_q, register_22_q, register_23_q, register_24_q, register_25_q,
       register_26_q, register_27_q, register_28_q, register_29_q, register_30_q, register_31_q,
       register_32_q;

  Decoder #(.select(5), .enable("false")) decoder_1 (
    .out0(decoder_1_out0), .out1(decoder_1_out1), .out2(decoder_1_out2), .out3(decoder_1_out3),
    .out4(decoder_1_out4), .out5(decoder_1_out5), .out6(decoder_1_out6), .out7(decoder_1_out7),
    .out8(decoder_1_out8), .out9(decoder_1_out9), .out10(decoder_1_out10), .out11(decoder_1_out11),
    .out12(decoder_1_out12), .out13(decoder_1_out13), .out14(decoder_1_out14), .out15(decoder_1_out15),
    .out16(decoder_1_out16), .out17(decoder_1_out17), .out18(decoder_1_out18), .out19(decoder_1_out19),
    .out20(decoder_1_out20), .out21(decoder_1_out21), .out22(decoder_1_out22), .out23(decoder_1_out23),
    .out24(decoder_1_out24), .out25(decoder_1_out25), .out26(decoder_1_out26), .out27(decoder_1_out27),
    .out28(decoder_1_out28), .out29(decoder_1_out29), .out30(decoder_1_out30), .out31(decoder_1_out31),
    .sel(Read_Write));
  Decoder #(.enable("false")) decoder_2 (.out0(decoder_2_out0), .out1(decoder_2_out1), .sel(Escreve_Registrador));
  not not_1 (not_1_out, Enable);
  Register #(.width(32)) register_1 (.D(Dados_para_escrita), .en(_0_out), .Q(register_1_q), .clk(CLK), .clr(not_1_out));
  and _0 (_0_out, decoder_1_out0, decoder_2_out1);
  Register #(.width(32)) register_2 (.D(Dados_para_escrita), .en(_8_out), .Q(register_2_q), .clk(CLK), .clr(not_1_out));
  and _8 (_8_out, decoder_1_out8, decoder_2_out1);
  Register #(.width(32)) register_3 (
    .D(Dados_para_escrita), .en(_16_out), .Q(register_3_q), .clk(CLK), .clr(not_1_out));
  and _16 (_16_out, decoder_1_out16, decoder_2_out1);
  Register #(.width(32)) register_4 (
    .D(Dados_para_escrita), .en(_24_out), .Q(register_4_q), .clk(CLK), .clr(not_1_out));
  and _24 (_24_out, decoder_1_out24, decoder_2_out1);
  and _1 (_1_out, decoder_1_out1, decoder_2_out1);
  and _9 (_9_out, decoder_1_out9, decoder_2_out1);
  and _17 (_17_out, decoder_1_out17, decoder_2_out1);
  and _25 (_25_out, decoder_1_out25, decoder_2_out1);
  Register #(.width(32)) register_5 (.D(Dados_para_escrita), .en(_1_out), .Q(register_5_q), .clk(CLK), .clr(not_1_out));
  Register #(.width(32)) register_6 (.D(Dados_para_escrita), .en(_9_out), .Q(register_6_q), .clk(CLK), .clr(not_1_out));
  Register #(.width(32)) register_7 (
    .D(Dados_para_escrita), .en(_17_out), .Q(register_7_q), .clk(CLK), .clr(not_1_out));
  Register #(.width(32)) register_8 (
    .D(Dados_para_escrita), .en(_25_out), .Q(register_8_q), .clk(CLK), .clr(not_1_out));
  and _2 (_2_out, decoder_1_out2, decoder_2_out1);
  and _10 (_10_out, decoder_1_out10, decoder_2_out1);
  and _18 (_18_out, decoder_1_out18, decoder_2_out1);
  and _26 (_26_out, decoder_1_out26, decoder_2_out1);
  Register #(.width(32)) register_9 (.D(Dados_para_escrita), .en(_2_out), .Q(register_9_q), .clk(CLK), .clr(not_1_out));
  Register #(.width(32)) register_10 (
    .D(Dados_para_escrita), .en(_10_out), .Q(register_10_q), .clk(CLK), .clr(not_1_out));
  Register #(.width(32)) register_11 (
    .D(Dados_para_escrita), .en(_18_out), .Q(register_11_q), .clk(CLK), .clr(not_1_out));
  Register #(.width(32)) register_12 (
    .D(Dados_para_escrita), .en(_26_out), .Q(register_12_q), .clk(CLK), .clr(not_1_out));
  and _3 (_3_out, decoder_1_out3, decoder_2_out1);
  and _11 (_11_out, decoder_1_out11, decoder_2_out1);
  and _19 (_19_out, decoder_1_out19, decoder_2_out1);
  and _27 (_27_out, decoder_1_out27, decoder_2_out1);
  Register #(.width(32)) register_13 (
    .D(Dados_para_escrita), .en(_3_out), .Q(register_13_q), .clk(CLK), .clr(not_1_out));
  Register #(.width(32)) register_14 (
    .D(Dados_para_escrita), .en(_11_out), .Q(register_14_q), .clk(CLK), .clr(not_1_out));
  Register #(.width(32)) register_15 (
    .D(Dados_para_escrita), .en(_19_out), .Q(register_15_q), .clk(CLK), .clr(not_1_out));
  Register #(.width(32)) register_16 (
    .D(Dados_para_escrita), .en(_27_out), .Q(register_16_q), .clk(CLK), .clr(not_1_out));
  and _4 (_4_out, decoder_1_out4, decoder_2_out1);
  and _12 (_12_out, decoder_1_out12, decoder_2_out1);
  and _20 (_20_out, decoder_1_out20, decoder_2_out1);
  and _28 (_28_out, decoder_1_out28, decoder_2_out1);
  Register #(.width(32)) register_17 (
    .D(Dados_para_escrita), .en(_4_out), .Q(register_17_q), .clk(CLK), .clr(not_1_out));
  Register #(.width(32)) register_18 (
    .D(Dados_para_escrita), .en(_12_out), .Q(register_18_q), .clk(CLK), .clr(not_1_out));
  Register #(.width(32)) register_19 (
    .D(Dados_para_escrita), .en(_20_out), .Q(register_19_q), .clk(CLK), .clr(not_1_out));
  Register #(.width(32)) register_20 (
    .D(Dados_para_escrita), .en(_28_out), .Q(register_20_q), .clk(CLK), .clr(not_1_out));
  and _5 (_5_out, decoder_1_out5, decoder_2_out1);
  and _13 (_13_out, decoder_1_out13, decoder_2_out1);
  and _21 (_21_out, decoder_1_out21, decoder_2_out1);
  and _29 (_29_out, decoder_1_out29, decoder_2_out1);
  Register #(.width(32)) register_21 (
    .D(Dados_para_escrita), .en(_5_out), .Q(register_21_q), .clk(CLK), .clr(not_1_out));
  Register #(.width(32)) register_22 (
    .D(Dados_para_escrita), .en(_13_out), .Q(register_22_q), .clk(CLK), .clr(not_1_out));
  Register #(.width(32)) register_23 (
    .D(Dados_para_escrita), .en(_21_out), .Q(register_23_q), .clk(CLK), .clr(not_1_out));
  Register #(.width(32)) register_24 (
    .D(Dados_para_escrita), .en(_29_out), .Q(register_24_q), .clk(CLK), .clr(not_1_out));
  and _6 (_6_out, decoder_1_out6, decoder_2_out1);
  and _14 (_14_out, decoder_1_out14, decoder_2_out1);
  and _22 (_22_out, decoder_1_out22, decoder_2_out1);
  and _30 (_30_out, decoder_1_out30, decoder_2_out1);
  Register #(.width(32)) register_25 (
    .D(Dados_para_escrita), .en(_6_out), .Q(register_25_q), .clk(CLK), .clr(not_1_out));
  Register #(.width(32)) register_26 (
    .D(Dados_para_escrita), .en(_14_out), .Q(register_26_q), .clk(CLK), .clr(not_1_out));
  Register #(.width(32)) register_27 (
    .D(Dados_para_escrita), .en(_22_out), .Q(register_27_q), .clk(CLK), .clr(not_1_out));
  Register #(.width(32)) register_28 (
    .D(Dados_para_escrita), .en(_30_out), .Q(register_28_q), .clk(CLK), .clr(not_1_out));
  Register #(.width(32)) register_29 (
    .D(Dados_para_escrita), .en(_7_out), .Q(register_29_q), .clk(CLK), .clr(not_1_out));
  and _7 (_7_out, decoder_1_out7, decoder_2_out1);
  Register #(.width(32)) register_30 (
    .D(Dados_para_escrita), .en(_15_out), .Q(register_30_q), .clk(CLK), .clr(not_1_out));
  and _15 (_15_out, decoder_1_out15, decoder_2_out1);
  Register #(.width(32)) register_31 (
    .D(Dados_para_escrita), .en(_23_out), .Q(register_31_q), .clk(CLK), .clr(not_1_out));
  and _23 (_23_out, decoder_1_out23, decoder_2_out1);
  Register #(.width(32)) register_32 (
    .D(Dados_para_escrita), .en(_31_out), .Q(register_32_q), .clk(CLK), .clr(not_1_out));
  and _31 (_31_out, decoder_1_out31, decoder_2_out1);
  Multiplexer #(.select(5), .width(32)) multiplexer_1 (
    .in0(register_1_q), .in1(register_5_q), .in2(register_9_q), .in3(register_13_q), .in4(register_17_q),
    .in5(register_21_q), .in6(register_25_q), .in7(register_29_q), .in8(register_2_q), .in9(register_6_q),
    .in10(register_10_q), .in11(register_14_q), .in12(register_18_q), .in13(register_22_q),
    .in14(register_26_q), .in15(register_30_q), .in16(register_3_q), .in17(register_7_q),
    .in18(register_11_q), .in19(register_15_q), .in20(register_19_q), .in21(register_23_q),
    .in22(register_27_q), .in23(register_31_q), .in24(register_4_q), .in25(register_8_q),
    .in26(register_12_q), .in27(register_16_q), .in28(register_20_q), .in29(register_24_q),
    .in30(register_28_q), .in31(register_32_q), .out(Dados_de_Leitura_1), .sel(Read_Reg_1),
    .en(decoder_2_out0));
  Multiplexer #(.select(5), .width(32)) multiplexer_2 (
    .in0(register_1_q), .in1(register_5_q), .in2(register_9_q), .in3(register_13_q), .in4(register_17_q),
    .in5(register_21_q), .in6(register_25_q), .in7(register_29_q), .in8(register_2_q), .in9(register_6_q),
    .in10(register_10_q), .in11(register_14_q), .in12(register_18_q), .in13(register_22_q),
    .in14(register_26_q), .in15(register_30_q), .in16(register_3_q), .in17(register_7_q),
    .in18(register_11_q), .in19(register_15_q), .in20(register_19_q), .in21(register_23_q),
    .in22(register_27_q), .in23(register_31_q), .in24(register_4_q), .in25(register_8_q),
    .in26(register_12_q), .in27(register_16_q), .in28(register_20_q), .in29(register_24_q),
    .in30(register_28_q), .in31(register_32_q), .out(Dados_de_Leitura_2), .sel(Read_Reg_2),
    .en(decoder_2_out0));
endmodule

module Mem_Dados (
  input  Le_Mem,
  input  Clock,
  input  Escreve_Mem,
  input  [31:0] Resultado_da_ALU,
  input  Enable,
  input  [31:0] Entrada_de_Dados,
  output [31:0] Output
);

  wire multiplexer_1_out, not_1_out, not_2_out, or_1_out;

  not not_1 (not_1_out, Clock);
  Multiplexer #(.enable("false")) multiplexer_1 (
    .in0(Clock), .in1(not_1_out), .out(multiplexer_1_out), .sel(Escreve_Mem));
  or or_1 (or_1_out, Escreve_Mem, Le_Mem);
  RAM #(.addrWidth(24), .dataWidth(32), .bus("separate")) ram_1 (
    .addr(Resultado_da_ALU[23:0]), .din(Entrada_de_Dados), .data(Output), .str(Escreve_Mem), .sel(or_1_out),
    .clk(multiplexer_1_out), .ld(Le_Mem), .clr(not_2_out));
  not not_2 (not_2_out, Enable);
  // also tied to GND on the sheet: {Resultado_da_ALU[24], Resultado_da_ALU[25], Resultado_da_ALU[26], Resultado_da_ALU[27], Resultado_da_ALU[28], Resultado_da_ALU[29], Resultado_da_ALU[30], Resultado_da_ALU[31]}
endmodule

module unidade_controle (
  input  [5:0] \Instrução ,
  input  Enable,
  output RegDst,
  output ALUSrc,
  output MemToReg,
  output RegWrite,
  output MemRead,
  output MemWrite,
  output Branch,
  output [1:0] OpALU,
  output Branch_Not_Equal,
  output Jump,
  output Clock,
  output AtuaPC
);

  wire and_1_out, and_2_out, and_3_out, and_4_out, and_5_out, and_8_out, clock_1_out, nand_1_out, not_1_out,
       not_2_out, or_1_out, or_2_out, or_3_out, or_4_out;
  wire [1:0] counter_1_q;

  and and_1 (and_1_out, ~\Instrução [0], ~\Instrução [1], \Instrução [2], ~\Instrução [3], ~\Instrução [4], ~\Instrução [5]);  // AND_Gate
  and and_2 (and_2_out, ~\Instrução [0], ~\Instrução [1], ~\Instrução [2], ~\Instrução [3], ~\Instrução [4], ~\Instrução [5]);  // AND_Gate
  and and_3 (and_3_out, \Instrução [0], ~\Instrução [1], ~\Instrução [2], ~\Instrução [3], \Instrução [4], \Instrução [5]);  // AND_Gate
  and and_4 (and_4_out, \Instrução [0], ~\Instrução [1], \Instrução [2], ~\Instrução [3], \Instrução [4], \Instrução [5]);  // AND_Gate
  and and_5 (and_5_out, ~\Instrução [0], ~\Instrução [1], ~\Instrução [2], \Instrução [3], ~\Instrução [4], ~\Instrução [5]);  // AND_Gate
  and and_6 (Jump, ~\Instrução [0], ~\Instrução [1], ~\Instrução [2], ~\Instrução [3], \Instrução [4], ~\Instrução [5]);  // AND_Gate
  and and_7 (Branch_Not_Equal, ~\Instrução [0], ~\Instrução [1], ~\Instrução [2], \Instrução [3], ~\Instrução [4], \Instrução [5]);  // AND_Gate
  and and_8 (and_8_out, \Instrução [0], \Instrução [1], \Instrução [2], \Instrução [3], \Instrução [4], \Instrução [5]);
  not not_1 (not_1_out, and_8_out);
  Clock clock_1 (.out(clock_1_out));
  or or_1 (or_1_out, and_5_out, Branch_Not_Equal);
  and and_9 (Clock, not_1_out, clock_1_out, Enable);
  or or_2 (or_2_out, and_3_out, and_1_out, and_4_out);
  or or_3 (or_3_out, and_3_out, and_1_out, and_2_out);
  not not_2 (not_2_out, Enable);
  Counter #(.width(2), .max('h3)) counter_1 (
    .Q(counter_1_q), .clk(Clock), .clr(not_2_out));  // open: load, D, count, carry
  nand nand_1 (nand_1_out, counter_1_q[0], ~counter_1_q[1]);  // NAND_Gate
  or or_4 (or_4_out, counter_1_q[0], counter_1_q[1]);
  and and_10 (RegDst, ~Jump, or_4_out, and_2_out);  // AND_Gate
  and and_11 (ALUSrc, ~Jump, or_4_out, or_2_out);  // AND_Gate
  and and_12 (MemToReg, ~Jump, or_4_out, and_3_out);  // AND_Gate
  and and_13 (RegWrite, ~Jump, or_4_out, nand_1_out, or_3_out);  // AND_Gate
  and and_14 (MemRead, ~Jump, or_4_out, and_3_out);  // AND_Gate
  and and_15 (MemWrite, ~Jump, or_4_out, and_4_out);  // AND_Gate
  and and_16 (Branch, ~Jump, or_4_out, or_1_out);  // AND_Gate
  and and_17 (OpALU[0], ~Jump, or_4_out, and_2_out);  // AND_Gate
  and and_18 (OpALU[1], ~Jump, or_4_out, or_1_out);  // AND_Gate
  not not_3 (AtuaPC, or_4_out);

  // Notes on the sheet:
  //   TIPO I
  //   TIPO R
  //   LW
  //   SW
  //   BEQ
  //   JUMP
  //   BNE
  //   ALUop1
  //   ALUop0
endmodule

module ALU2 (
  input  [31:0] B,
  input  [31:0] A,
  input  [2:0] in_3,
  input  Enable,
  input  Clock,
  output [31:0] Result,
  output Zero
);

  wire and_2_out, not_1_out, not_2_out;
  wire [1:0] counter_1_q;
  wire [31:0] adder_1_out, and_1_out, multiplexer_1_out, or_1_out, subtractor_1_out;

  Adder #(.width(32)) adder_1 (.a(A), .b(B), .out(adder_1_out));  // open: cin, cout
  Subtractor #(.width(32)) subtractor_1 (.a(A), .b(B), .out(subtractor_1_out));  // open: bin, bout
  Multiplier #(.width(32)) multiplier_1 (.a(A), .b(B));  // open: out, cin, cout
  assign and_1_out = A & B;  // AND_Gate and_1, 32 bits wide
  assign or_1_out = A | B;  // OR_Gate or_1, 32 bits wide
  Multiplexer #(.select(3), .width(32), .enable("false")) multiplexer_1 (
    .in0(adder_1_out), .in6(subtractor_1_out), .out(multiplexer_1_out), .sel(in_3));  // open: in1, in2, in3, in4, in5, in7
  nor nor_1 (Zero, multiplexer_1_out[0], multiplexer_1_out[1], multiplexer_1_out[2], multiplexer_1_out[3], multiplexer_1_out[4], multiplexer_1_out[5], multiplexer_1_out[6], multiplexer_1_out[7], multiplexer_1_out[8], multiplexer_1_out[9], multiplexer_1_out[10], multiplexer_1_out[11], multiplexer_1_out[12], multiplexer_1_out[13], multiplexer_1_out[14], multiplexer_1_out[15], multiplexer_1_out[16], multiplexer_1_out[17], multiplexer_1_out[18], multiplexer_1_out[19], multiplexer_1_out[20], multiplexer_1_out[21], multiplexer_1_out[22], multiplexer_1_out[23], multiplexer_1_out[24], multiplexer_1_out[25], multiplexer_1_out[26], multiplexer_1_out[27], multiplexer_1_out[28], multiplexer_1_out[29], multiplexer_1_out[30], multiplexer_1_out[31]);
  Counter #(.width(2), .max('h3)) counter_1 (
    .Q(counter_1_q), .clk(Clock), .clr(not_1_out));  // open: load, D, count, carry
  not not_1 (not_1_out, Enable);
  RAM #(.addrWidth(2), .dataWidth(32), .bus("separate")) ram_1 (
    .addr(counter_1_q), .din(multiplexer_1_out), .data(Result), .str(and_2_out), .sel(Clock), .clk(Clock),
    .ld(not_2_out));  // open: clr
  not not_2 (not_2_out, and_2_out);
  and and_2 (and_2_out, counter_1_q[1], ~counter_1_q[0]);  // AND_Gate
endmodule

module ALU_Control_2 (
  input  [1:0] OPcode,
  input  [5:0] Funct,
  output [2:0] out_3
);

  wire add_out, and_1_out, and_3_out, and_4_out, sub_out;
  wire [2:0] and_5_out, and_6_out, and_7_out, and_8_out, and_9_out;
  wire [2:2] and_2_out, mult_out, OR_2_out, or_3_out, or_4_out, OR_out;

  and add (add_out, and_1_out, ~Funct[0], ~Funct[1], ~Funct[2], ~Funct[3], ~Funct[4], Funct[5]);  // AND_Gate
  and sub (sub_out, and_1_out, ~Funct[0], Funct[1], ~Funct[2], ~Funct[3], ~Funct[4], Funct[5]);  // AND_Gate
  and mult (mult_out[2], and_1_out, ~Funct[0], ~Funct[1], ~Funct[2], Funct[3], Funct[4], ~Funct[5]);  // AND_Gate
  and and_1 (and_1_out, ~OPcode[0], OPcode[1]);  // AND_Gate
  and and_2 (and_2_out[2], and_1_out, ~Funct[0], ~Funct[1], Funct[2], ~Funct[3], ~Funct[4], Funct[5]);  // AND_Gate
  and OR (OR_out[2], and_1_out, Funct[0], ~Funct[1], Funct[2], ~Funct[3], ~Funct[4], Funct[5]);  // AND_Gate
  and OR_2 (OR_2_out[2], and_1_out, ~Funct[0], Funct[1], ~Funct[2], Funct[3], ~Funct[4], Funct[5]);  // AND_Gate
  and and_3 (and_3_out, ~OPcode[1], ~OPcode[1]);  // AND_Gate
  and and_4 (and_4_out, OPcode[1], ~OPcode[1]);  // AND_Gate
  or or_3 (or_3_out[2], and_3_out, add_out);
  or or_4 (or_4_out[2], and_4_out, sub_out);
  assign and_5_out = 3'b000 & {3{or_3_out[2]}};  // AND_Gate and_5, 3 bits wide
  assign and_6_out = 3'b001 & {3{or_4_out[2]}};  // AND_Gate and_6, 3 bits wide
  assign and_7_out = 3'b010 & {3{mult_out[2]}};  // AND_Gate and_7, 3 bits wide
  assign and_8_out = 3'b011 & {3{and_2_out[2]}};  // AND_Gate and_8, 3 bits wide
  assign and_9_out = 3'b100 & {3{OR_out[2]}};  // AND_Gate and_9, 3 bits wide
  // AND_Gate and_10 has open pins: in0=3'b111, in1={3{OR_2_out[2]}}, out=open
  assign out_3 = and_5_out | and_6_out | and_7_out | and_8_out | and_9_out;  // OR_Gate or_5, 3 bits wide

  // Notes on the sheet:
  //   100000
  //   100010
  //   011000
  //   tipo r
  //   100100
  //   100101
  //   101010
  //   lw/sw
  //   branch equal
endmodule

module PC (
  input  [25:0] INPUT,
  input  Controle_Jump,
  input  Zero___Branch,
  input  [31:0] Resultado_ALU,
  input  AtuaPC,
  output [31:0] PC
);

  wire Reset_out;
  wire [31:0] adder_1_out, adder_2_out, multiplexer_1_out, multiplexer_2_out;

  Adder #(.width(32)) adder_1 (.a(32'h1), .b(PC), .out(adder_1_out));  // open: cin, cout
  Register #(.width(32)) register_1 (.D(multiplexer_2_out), .Q(PC), .clk(AtuaPC), .clr(Reset_out));  // open: en
  Button Reset (.out(Reset_out));
  Adder #(.width(32)) adder_2 (.a(adder_1_out), .b(Resultado_ALU), .out(adder_2_out));  // open: cin, cout
  Multiplexer #(.width(32), .enable("false")) multiplexer_1 (
    .in0(adder_1_out), .in1(adder_2_out), .out(multiplexer_1_out), .sel(Zero___Branch));
  Multiplexer #(.width(32), .enable("false")) multiplexer_2 (
    .in0(multiplexer_1_out), .in1({2'b00, adder_1_out[29:26], INPUT}), .out(multiplexer_2_out),
    .sel(Controle_Jump));
endmodule

module Completo (
  input  Enable,
  output [5:0] out_2,
  output [31:0] out_3,
  output out_4,
  output [31:0] out_5,
  output [31:0] out_6,
  output [4:0] out_7,
  output [4:0] out_8,
  output [31:0] out_9,
  output [31:0] out_10,
  output [4:0] out_11,
  output [4:0] out_12,
  output [25:0] out_13,
  output [31:0] out_14,
  output [5:0] out_15,
  output [2:0] out_16
);

  wire and_1_out, multiplexer_3_out, not_1_out, not_2_out, unidade_controle_1_alusrc,
       unidade_controle_1_atuapc, unidade_controle_1_branch, unidade_controle_1_branch_not_equal,
       unidade_controle_1_clock, unidade_controle_1_jump, unidade_controle_1_memread,
       unidade_controle_1_memtoreg, unidade_controle_1_memwrite, unidade_controle_1_regdst,
       unidade_controle_1_regwrite;
  wire [1:0] unidade_controle_1_opalu;
  wire [15:0] mem_instr_2_1_immediate;
  wire [31:0] banco_registrador_1_dados_de_leitura_2, bit_extender_1_out;

  PC pc_1 (
    .INPUT(out_13), .Resultado_ALU(bit_extender_1_out), .AtuaPC(unidade_controle_1_atuapc), .PC(out_14),
    .Controle_Jump(unidade_controle_1_jump), .Zero___Branch(and_1_out));
  Mem_instr_2 mem_instr_2_1 (
    .PC(out_14), .OPCODE(out_2), .RS(out_7), .RT(out_8), .RD(out_12), .FUNCT(out_15),
    .IMMEDIATE(mem_instr_2_1_immediate), .ADDRESS(out_13), .AtuaPC(unidade_controle_1_atuapc), .Enable(Enable));
  Multiplexer #(.width(5), .enable("false")) multiplexer_1 (
    .in0(out_8), .in1(out_12), .out(out_11), .sel(unidade_controle_1_regdst));
  unidade_controle unidade_controle_1 (
    .Enable(Enable), .RegDst(unidade_controle_1_regdst), .ALUSrc(unidade_controle_1_alusrc),
    .MemToReg(unidade_controle_1_memtoreg), .RegWrite(unidade_controle_1_regwrite),
    .MemRead(unidade_controle_1_memread), .MemWrite(unidade_controle_1_memwrite),
    .Branch(unidade_controle_1_branch), .OpALU(unidade_controle_1_opalu), .Jump(unidade_controle_1_jump),
    .Clock(unidade_controle_1_clock), .AtuaPC(unidade_controle_1_atuapc), .\Instrução (out_2),
    .Branch_Not_Equal(unidade_controle_1_branch_not_equal));
  assign bit_extender_1_out = {{16{mem_instr_2_1_immediate[15]}}, mem_instr_2_1_immediate};  // Bit_Extender bit_extender_1
  Banco_registrador banco_registrador_1 (
    .Read_Reg_1(out_7), .Read_Reg_2(out_8), .Enable(Enable), .Dados_de_Leitura_1(out_5),
    .Dados_de_Leitura_2(banco_registrador_1_dados_de_leitura_2), .Read_Write(out_11),
    .Escreve_Registrador(unidade_controle_1_regwrite), .CLK(unidade_controle_1_clock),
    .Dados_para_escrita(out_9));
  Multiplexer #(.width(32), .enable("false")) multiplexer_2 (
    .in0(banco_registrador_1_dados_de_leitura_2), .in1(bit_extender_1_out), .out(out_6),
    .sel(unidade_controle_1_alusrc));
  ALU_Control alu_control_1 (.FUNCAO(out_15), .OPCode(unidade_controle_1_opalu), .Result(out_16));
  ALU alu_1 (.A(out_5), .B(out_6), .RESULTADO(out_10), .Zero(out_4), .Operacao(out_16));
  Multiplexer #(.enable("false")) multiplexer_3 (
    .in0(out_4), .in1(not_1_out), .out(multiplexer_3_out), .sel(unidade_controle_1_branch_not_equal));
  not not_1 (not_1_out, out_4);
  and and_1 (and_1_out, unidade_controle_1_branch, multiplexer_3_out);
  Mem_Dados mem_dados_1 (
    .Resultado_da_ALU(out_10), .Entrada_de_Dados(banco_registrador_1_dados_de_leitura_2), .Output(out_3),
    .Enable(Enable), .Le_Mem(unidade_controle_1_memread), .Clock(unidade_controle_1_clock),
    .Escreve_Mem(unidade_controle_1_memwrite));
  not not_2 (not_2_out, unidade_controle_1_memtoreg);
  Multiplexer #(.width(32), .enable("false")) multiplexer_4 (.in0(out_3), .in1(out_10), .out(out_9), .sel(not_2_out));
endmodule

module Mem_instr_2 (
  input  [31:0] PC,
  input  AtuaPC,
  input  Enable,
  output [5:0] OPCODE,
  output [4:0] RS,
  output [4:0] RT,
  output [4:0] RD,
  output [5:0] FUNCT,
  output [15:0] IMMEDIATE,
  output [25:0] ADDRESS
);

  wire button_1_out, or_1_out;
  wire [23:0] bitselector_1_out;

  BitSelector #(.width(32), .group(24)) bitselector_1 (.in(PC), .out(bitselector_1_out), .sel(1'b0));
  or or_1 (or_1_out, AtuaPC, Enable);
  Button button_1 (.out(button_1_out));
  RAM #(.addrWidth(24), .dataWidth(32), .bus("separate")) ram_1 (
    .addr(bitselector_1_out), .data({OPCODE, ADDRESS}), .clk(or_1_out), .clr(button_1_out));  // open: din, str, sel, ld

  assign FUNCT = ADDRESS[5:0];
  assign IMMEDIATE = ADDRESS[15:0];
  assign RD = ADDRESS[15:11];
  assign RS = ADDRESS[25:21];
  assign RT = ADDRESS[20:16];
endmodule
